# Fritzing sketch 106 pcb (saved by Fritzing 0.9.3b)
circuit board: 8.46667cm x 5.64444cm
breadboards: 1

parts:
  元件1 = Arduino Uno (Rev3)
  R1 = Resistor [tolerance=±5% resistance=10k package=THT]
  Q1 = npn-Powertransistor [package="TO220 [THT]"]
  BAT2 = BC9VPC [package=bc9vpc]
  S1 = Reed switch [package=THT]
  L1 = Solenoid
  J1 = Basic Servo
  Grove1 = Grove 3 Axis Digital Accelerometer 16g
  U1 = DC-DC_CONVERTER [package=dc-dc_converter]

nets:
  N1: 元件1.A4/SDA, Grove1.SDA
  N2: 元件1.A5/SCL, Grove1.SCL
  N3: 元件1.D2, R1.Pin_1, Q1.base
  N4: 元件1.D3_PWM, J1.pulse
  N5: 元件1.D4, S1.pin_1
  5V: 元件1.5V, Grove1.VCC
  GND: 元件1.GND, R1.Pin_0, Q1.emitter, BAT2.V-, Grove1.GND, U1.GND1
  VIN: 元件1.VIN, BAT2.V+, L1.pin2, U1.VIN
  N6: Q1.collector, L1.pin1
  GND_2: J1.gnd, U1.GND2
  N7: J1.vcc, U1.VOUT

notes:
  12 V battery
  10 K resistor
  MOSFET
  reed switch
  Arduino UNO R3
  compass and accelormetor
  servo
  solenoid air vavle
  12DC to 6DC converter
